# Fritzing sketch robot_arduino_mega202212_AE-TB67H450 (saved by Fritzing 0.9.9b)
circuit board: 9.80001cm x 9.80001cm
breadboards: 1

parts:
  R1 = Resistor [tolerance=±5% resistance=1 power=0.25 package=THT]
  R2 = Resistor [tolerance=±5% resistance=1 power=0.25 package=THT]
  R3 = Resistor [tolerance=±5% resistance=1 power=0.25 package=THT]
  R4 = Resistor [tolerance=±5% resistance=1 power=0.25 package=THT]
  C42 = Ceramic Capacitor [capacitance=100nF voltage=35V package="100 mil [THT, multilayer]"]
  C41 = Ceramic Capacitor [capacitance=100nF voltage=35V package="100 mil [THT, multilayer]"]
  C12 = Ceramic Capacitor [capacitance=100nF voltage=35V package="100 mil [THT, multilayer]"]
  C13 = Electrolytic Capacitor [capacitance=0.1mF voltage=10V package="100 mil [THT, electrolytic]"]
  C11 = Ceramic Capacitor [capacitance=100nF voltage=35V package="100 mil [THT, multilayer]"]
  C21 = Ceramic Capacitor [capacitance=100nF voltage=35V package="100 mil [THT, multilayer]"]
  C22 = Ceramic Capacitor [capacitance=100nF voltage=35V package="100 mil [THT, multilayer]"]
  C23 = Electrolytic Capacitor [capacitance=0.1mF voltage=10V package="100 mil [THT, electrolytic]"]
  C31 = Ceramic Capacitor [capacitance=100nF voltage=35V package="100 mil [THT, multilayer]"]
  C32 = Ceramic Capacitor [capacitance=100nF voltage=35V package="100 mil [THT, multilayer]"]
  C33 = Electrolytic Capacitor [capacitance=0.1mF voltage=10V package="100 mil [THT, electrolytic]"]
  C43 = Electrolytic Capacitor [capacitance=0.1mF voltage=10V package="100 mil [THT, electrolytic]"]
  パーツ1 = Arduino Mega 2560 (Rev3)
  MT1 = JST XH 2A [form="♀ (female)" package=THT]
  MT2 = JST XH 2A [form="♀ (female)" package=THT]
  MT3 = JST XH 2A [form="♀ (female)" package=THT]
  BAT = JST XH 2A [form="♀ (female)" package=THT]
  MD4 = AE-TB67H450
  MD2 = AE-TB67H450
  MD3 = AE-TB67H450
  MD1 = AE-TB67H450
  OLED128x33 = I2C LCD 128x32 [package="DIP (Dual Inline) [THT]"]
  MPU6050 = MPU-6050 4pin [form="♀ (female)" package=THT]
  A3 = JST XH 3A [form="♀ (female)" package=THT]
  A7 = JST XH 3A [form="♀ (female)" package=THT]
  A11 = JST XH 3A [form="♀ (female)" package=THT]
  A13 = JST XH 3A [form="♀ (female)" package=THT]
  A15 = JST XH 3A [form="♀ (female)" package=THT]
  A1 = JST XH 3A [form="♀ (female)" package=THT]
  A4 = JST XH 3A [form="♀ (female)" package=THT]
  A8 = JST XH 3A [form="♀ (female)" package=THT]
  A6 = JST XH 3A [form="♀ (female)" package=THT]
  A9 = JST XH 3A [form="♀ (female)" package=THT]
  A10 = JST XH 3A [form="♀ (female)" package=THT]
  A2 = JST XH 3A [form="♀ (female)" package=THT]
  A12 = JST XH 3A [form="♀ (female)" package=THT]
  A0 = JST XH 3A [form="♀ (female)" package=THT]
  A14 = JST XH 3A [form="♀ (female)" package=THT]
  I2C1 = JST XH 4A [form="♀ (female)" package=THT]
  I2C2 = JST XH 4A [form="♀ (female)" package=THT]
  C1000u = Electrolytic Capacitor [capacitance=1mF voltage=16V package="200 mil [THT, electrolytic]"]
  LED45 = LED - 3mm [color="Red (633nm)" current=0.030 package="3 mm [THT]"]
  LED47 = LED - 3mm [color="Red (633nm)" current=0.030 package="3 mm [THT]"]
  LED49 = LED - 3mm [color="Red (633nm)" current=0.030 package="3 mm [THT]"]
  R1K = Resistor [tolerance=±5% power=0.25 resistance=1k package=THT]
  R1K_2 = Resistor [tolerance=±5% power=0.25 resistance=1k package=THT]
  R1K_3 = Resistor [tolerance=±5% power=0.25 resistance=1k package=THT]
  PWR_ON = LED - 3mm [color="Red (633nm)" current=0.030 package="3 mm [THT]"]
  R1K_4 = Resistor [tolerance=±5% power=0.25 resistance=1k package=THT]
  PTC = Resettable Fuse PTC [package=ptc]
  R10K = Resistor [tolerance=±5% power=0.25 resistance=10k package=THT]
  Pch = Basic FET P-Channel [package="TO220 [THT]"]
  PWR_SW = Toggle Switch [package=THT]
  RESET = Pushbutton [package="[THT]"]
  MT4 = JST XH 2A [form="♀ (female)" package=THT]
  A5 = JST XH 3A [form="♀ (female)" package=THT]
  TA4805S1 = Voltage Regulator - 5V [package="TO220 [THT]"]
  104 = Ceramic Capacitor [capacitance=0.1µF voltage=35V package="100 mil [THT, multilayer]"]
  C33u = Electrolytic Capacitor [capacitance=33µF voltage=10V package="100 mil [THT, electrolytic]"]
  U1 = JST XH 4A [form="♀ (female)" package=THT]
  U2 = JST XH 4A [form="♀ (female)" package=THT]
  U3 = JST XH 4A [form="♀ (female)" package=THT]
  U4 = JST XH 4A [form="♀ (female)" package=THT]
  SB = Schottky Diode [part_number=1N5817 package="300 mil [THT]"]
  Sensor1 = AE-BNO055-BO [part_number=AE-BNO055-BO]
  SW3(53) = Pushbutton [package="[THT]"]
  SW2(52) = Pushbutton [package="[THT]"]
  SW1(51) = Pushbutton [package="[THT]"]
  MT_SW = Toggle Switch [package=THT]
  R3_9K = Resistor [tolerance=±5% power=0.25 resistance=3.9k package=THT]
  R2K = Resistor [tolerance=±5% power=0.25 resistance=2k package=THT]

nets:
  N1: R1.Pin_0, MD1.RS
  GND: R1.Pin_1, R2.Pin_1, R3.Pin_1, R4.Pin_1, C42.0, C41.0, C12.0, C13.-, C11.0, C21.0, C22.0, C23.-, C31.0, C32.0, C33.-, C43.-, パーツ1.GND, BAT.pin2, MD4.GND, MD2.GND, MD3.GND, MD1.GND, OLED128x33.GND, MPU6050.pin2, A3.pin3, A7.pin3, A11.pin3, A13.pin3, A15.pin3, A1.pin3, A4.pin3, A8.pin3, A6.pin3, A9.pin3, A10.pin3, A2.pin3, A12.pin3, A0.pin3, A14.pin3, I2C1.pin4, I2C2.pin4, C1000u.-, R1K.Pin_1, R1K_2.Pin_1, R1K_3.Pin_1, R1K_4.Pin_1, PWR_SW.COM, PWR_SW.L2, RESET.Pin_1, RESET.Pin_2, A5.pin3, TA4805S1.GND, 104.0, C33u.-, U1.pin4, U2.pin4, U3.pin4, U4.pin4, Sensor1.GND, SW3(53).Pin_3, SW3(53).Pin_4, SW2(52).Pin_3, SW2(52).Pin_4, SW1(51).Pin_3, SW1(51).Pin_4, MT_SW.L2, R3_9K.Pin_1
  N2: R2.Pin_0, MD2.RS
  N3: R3.Pin_0, MD3.RS
  N4: R4.Pin_0, MD4.RS
  7.2V: C42.1, C12.1, C13.+, C22.1, C23.+, C32.1, C33.+, C43.+, パーツ1.VIN, MD4.VM, MD2.VM, MD3.VM, MD1.VM, Pch.drain, SB.anode
  3.4V: C41.1, C11.1, C21.1, C31.1, MD4.VREF, MD2.VREF, MD3.VREF, MD1.VREF, MT_SW.COM
  A8: パーツ1.A8, A8.pin1
  A9: パーツ1.A9, A9.pin1
  A10: パーツ1.A10, A10.pin1
  A11: パーツ1.A11, A11.pin1
  A12: パーツ1.A12, A12.pin1
  A13: パーツ1.A13, A13.pin1
  A14: パーツ1.A14, A14.pin1
  A15: パーツ1.A15, A15.pin1
  A0: パーツ1.A0, A0.pin1
  A1: パーツ1.A1, A1.pin1
  A2: パーツ1.A2, A2.pin1
  A3: パーツ1.A3, A3.pin1
  A4: パーツ1.A4, A4.pin1
  A5: パーツ1.A5, A5.pin1
  A6: パーツ1.A6, A6.pin1
  A7: パーツ1.A7, A7.pin1
  SCL: パーツ1.D21/SCL, パーツ1.SCL, OLED128x33.SCL, MPU6050.pin3, I2C1.pin1, I2C2.pin1, Sensor1.SCL/R
  SDA: パーツ1.D20/SDA, パーツ1.SDA, OLED128x33.SDA, MPU6050.pin4, I2C1.pin3, I2C2.pin3, Sensor1.SDA/T
  D-IN2: パーツ1.D9_PWM, MD4.IN2
  D-IN1: パーツ1.D8_PWM, MD4.IN1
  N5: パーツ1.RESET, RESET.Pin_3, RESET.Pin_4
  3.3V: パーツ1.3V3
  5V: パーツ1.5V, OLED128x33.VCC, MPU6050.pin1, A3.pin2, A7.pin2, A11.pin2, A13.pin2, A15.pin2, A1.pin2, A4.pin2, A8.pin2, A6.pin2, A9.pin2, A10.pin2, A2.pin2, A12.pin2, A0.pin2, A14.pin2, I2C1.pin2, I2C2.pin2, C1000u.+, PWR_ON.anode, A5.pin2, TA4805S1.output_voltage, C33u.+, U1.pin3, U2.pin3, U3.pin3, U4.pin3, Sensor1.VIN, R2K.Pin_0
  A-IN1: パーツ1.D2_PWM, MD1.IN1
  A-IN2: パーツ1.D3_PWM, MD1.IN2
  B-IN1: パーツ1.D4_PWM, MD2.IN1
  B-IN2: パーツ1.D5_PWM, MD2.IN2
  C-IN1: パーツ1.D6_PWM, MD3.IN1
  C-IN2: パーツ1.D7_PWM, MD3.IN2
  D29: パーツ1.D29, U4.pin1
  D31: パーツ1.D31, U4.pin2
  D33: パーツ1.D33, U3.pin1
  D35: パーツ1.D35, U3.pin2
  D37: パーツ1.D37, U2.pin1
  D39: パーツ1.D39, U2.pin2
  D41: パーツ1.D41, U1.pin1
  D43: パーツ1.D43, U1.pin2
  D45: パーツ1.D45, LED45.anode
  D47: パーツ1.D47, LED47.anode
  D49: パーツ1.D49, LED49.anode
  SW1: パーツ1.D51, SW1(51).Pin_1, SW1(51).Pin_2
  SW2: パーツ1.D52, SW2(52).Pin_1, SW2(52).Pin_2
  SW3: パーツ1.D53, SW3(53).Pin_1, SW3(53).Pin_2
  N6: MT1.pin1, MD1.OUT1
  N7: MT1.pin2, MD1.OUT2
  N8: MT2.pin1, MD2.OUT1
  N9: MT2.pin2, MD2.OUT2
  N10: MT3.pin1, MD3.OUT1
  N11: MT3.pin2, MD3.OUT2
  N12: BAT.pin1, PTC.1
  N13: MD4.OUT1, MT4.pin1
  N14: MD4.OUT2, MT4.pin2
  N15: LED45.cathode, R1K_2.Pin_0
  N16: LED47.cathode, R1K.Pin_0
  N17: LED49.cathode, R1K_3.Pin_0
  N18: PWR_ON.cathode, R1K_4.Pin_0
  N19: PTC.2, R10K.Pin_0, Pch.source
  N20: R10K.Pin_1, Pch.gate, PWR_SW.L1
  N21: TA4805S1.input_voltage, 104.1, SB.cathode
  N22: MT_SW.L1, R3_9K.Pin_0, R2K.Pin_1

notes:
  BAT
  D13
  D12
  D11
  D10
  5V /BAT+
  -  -
  D1
  D5
  D2
  D3
  D7
  D6
  D0
  D4
  D9
  D8
  -
  +
  PWM
  SCL 5V SDA GND
  BAT+/ 5V
  D21
  D19
  D15
  D14
  D20
  D16
  D18
  D17
  I2C
  GND 5V D43 D41
  IN2:D3
  D48
  D50
  D46
  D44
  D42
  D40
  D38
  D36
  D34
  D32
  @ohguma 2022-12
  SELECT
  D22
  D24
  D26
  D28
  D30
  GND 5V D39 D37
  GND 5V D35 D33
  GND 5V D31 D29
  D52
  A2 A3 5V GND
  A0 5V GND
  A0 A1 5V GND
  A0 A1 A2 5V GND
  A4 A5 A6 5V GND
  A3 A4 5V GND
  A4 A5 5V GND
  A6 A7 5V GND
  A8 A9 A10 5V GND
  A7 A8 5V GND
  A8 A9 5V GND
  A10 A11 5V GND
  A11 A12 5V GND
  A12 A13 A14 5V GND
  A12 A13 5V GND
  A14 A15 5V GND
  D47
  D51
  D25
  D33
  D53
  D37
  D41
  D43
  D45
  D35
  D49
  D39
  D27
  D23
  D31
  D29
  GND
  5V
  AREF
  IN1:D2
  IN1:D4
  IN2:D5
  IN1:D6
  IN2:D7
  IN2:D9
  IN1:D8
  GND 5V
  D33 D35 5V GND
  D37 D39 5V GND
  D29 D31 5V GND
  D41 D43 5V GND
  S  D  G
  PWR SW
  RESET
  SW53
  SW52
  SW51
  5V GND BAT+
  MT SW
  MD Vref
  3V3
  1
  2
  3
  5V GND SCL SDA
  5V GND SDA SCL

custom parts:
  JST XH 2A: JST XH-2A
  AE-TB67H450: The TB67H450FNG is a PWM chopper type DC brushed motor driver. One channel of motor output block is embedded. Fabricated with the BiCD process, the TB67H450FNG is rated at output voltage 50 V, maximum current 3.5A.
  MPU-6050 4pin: Placa GY-521 basada en conjunto de acelerómetro+giroscopios MPU-6050 RafaG
  JST XH 3A: JST XH-3A
  JST XH 4A: JST XH-3A
  AE-BNO055-BO: VIN:3.3V or 5.V Interface:I2C or UART VOUT:2.8V Sensor:BNO-055 Size:18mm x 11mm
